# Fritzing sketch receiver (saved by Fritzing 0.9.9b)
breadboards: 1

parts:
  U1 = LM124-324 Quad Opamp [package="DIP (Dual Inline)"]
  R1 = Resistor [tolerance=±5% power=0.25 resistance=2k package=THT]
  R2 = Resistor [tolerance=±5% power=0.25 resistance=47.8k package=THT]
  R3 = Resistor [tolerance=±5% power=0.25 resistance=1.5k package=THT]
  R4 = Resistor [tolerance=±5% power=0.25 resistance=47.8k package=THT]
  R5 = Resistor [tolerance=±5% power=0.25 resistance=51k package=THT]
  R6 = Resistor [tolerance=±5% power=0.25 resistance=240 package=THT]
  R7 = Resistor [tolerance=±5% power=0.25 resistance=680 package=THT]
  C1 = Ceramic Capacitor [capacitance=10µF voltage=50V package="100 mil [THT, multilayer]"]
  C2 = Ceramic Capacitor [capacitance=10µF voltage=50V package="100 mil [THT, multilayer]"]
  C3 = Electrolytic Capacitor [capacitance=1µF voltage=35V package="100 mil [THT, electrolytic]"]
  C4 = Electrolytic Capacitor [capacitance=0.1µF voltage=35V package="100 mil [THT, electrolytic]"]
  D1 = Rectifier Diode [part_number=1N4001 package="300 mil [THT]"]
  C5 = Ceramic Capacitor [capacitance=0.1µF voltage=35V package="100 mil [THT, multilayer]"]
  C6 = Ceramic Capacitor [capacitance=100pF voltage=35V package="100 mil [THT, multilayer]"]
  C7 = Ceramic Capacitor [capacitance=2.2µF voltage=35V package="100 mil [THT, multilayer]"]
  U2 = Voltage Regulator [package=to220-adj]
  R8 = Resistor [tolerance=±5% power=0.25 resistance=1.2k package=THT]

nets (from the schematic view):
  N1: U1.1OUT, U1.2IN+, R8.Pin_1
  N2: U1.1IN-, C5.1, R8.Pin_0
  GND: U1.1IN+, U1.VCC-, R1.Pin_0, R3.Pin_1, R5.Pin_1, R7.Pin_0, C1.0, C2.0, C3.-, C4.-
  N3: U1.2IN-, R1.Pin_1, R2.Pin_0, C7.1
  N4: U1.2OUT, U1.3IN+, R2.Pin_1, C7.0
  N5: U1.3OUT, R4.Pin_1, D1.anode, C6.0
  N6: U1.3IN-, R3.Pin_0, R4.Pin_0, C6.1
  N7: R5.Pin_0, C1.1, C2.1, C4.+, D1.cathode, U2.IN
  N8: R6.Pin_0, R7.Pin_1, U2.ADJ
  N9: R6.Pin_1, C3.+, U2.OUT
